# Fritzing sketch relay_circuit (saved by Fritzing 0.9.3b)
breadboards: 1

parts:
  NPN = NPN-Transistor [package="TO92 [THT]"]
  10A_5v_Relay = RELAY [package=relay-jzc]
  R1 = Resistor [tolerance=±5% resistance=1k package=THT]
  Nicrome_Wire = FUSE [package=fuse_5mm]
  2s_Lipo = LIPO-110mAh [package=lipo-110]
  5v_Switching_Regulator = Voltage Regulator [package=78xxl]

nets:
  N1: NPN.E, Nicrome_Wire.2, 2s_Lipo.-, 5v_Switching_Regulator.GND
  N2: NPN.B, R1.Pin_1
  N3: NPN.C, 10A_5v_Relay.COIL2
  N4: 10A_5v_Relay.NO, Nicrome_Wire.1
  N5: 10A_5v_Relay.MAIN, 2s_Lipo.+, 5v_Switching_Regulator.IN
  N6: 10A_5v_Relay.COIL1, 5v_Switching_Regulator.OUT
